// Logisim project SequentialDivider.circ as structural Verilog: 1 circuit, main circuit Divider
module Divider (
  input  [3:0] Divisor,
  input  [3:0] Dividend,
  input  RESET,
  output [3:0] Quotient,
  output [3:0] Remainder,
  output DONE
);

  wire and_1_out, clock_1_out, counter_1_carry, not_1_out, not_2_out, not_3_out, not_4_out, not_11_out,
       not_12_out, or_1_out, shift_register_2_p7, shift_register_2_p8, shift_register_2_p9,
       shift_register_2_p10, shift_register_2_p11, subtractor_1_bout;
  wire [3:0] register_1_q;
  wire [7:0] multiplexer_1_out, shift_register_2_p16, subtractor_1_out;

  // Probe on Divisor
  Clock clock_1 (.out(clock_1_out));
  // Probe on Dividend
  not not_1 (not_1_out, RESET);
  not not_2 (not_2_out, RESET);
  not not_3 (not_3_out, RESET);
  not not_4 (not_4_out, RESET);
  Counter #(.max('h5), .width(4)) counter_1 (
    .load(RESET), .D(4'b0000), .carry(counter_1_carry), .up(1'b1), .clk(clock_1_out), .clr(RESET));  // open: count, Q
  // Shift_Register shift_register_1: pin names not known; wires that end beside it: RESET, clock_1_out, RESET, Divisor[3], Divisor[2], Divisor[1], Divisor[0], shift_register_2_p16[7], shift_register_2_p16[6], shift_register_2_p16[5]
  // Shift_Register #(.length(4)) shift_register_2: pin names not known; wires that end beside it: not_1_out, not_2_out, not_3_out, not_4_out, RESET, clock_1_out, shift_register_2_p7, shift_register_2_p8, shift_register_2_p9, shift_register_2_p10, shift_register_2_p11, shift_register_2_p16[4], shift_register_2_p16[3], shift_register_2_p16[2], shift_register_2_p16[1], shift_register_2_p16[0], Quotient[0], Quotient[1], Quotient[2], Quotient[3]
  // NOT_Gate not_5 has open pins: in=DONE, out=open
  not not_6 (shift_register_2_p7, subtractor_1_bout);
  not not_7 (shift_register_2_p8, RESET);
  not not_8 (shift_register_2_p9, RESET);
  not not_9 (shift_register_2_p10, RESET);
  not not_10 (shift_register_2_p11, RESET);
  D_Flip_Flop d_ff_1 (.clk(clock_1_out), .Q(DONE), .preset(counter_1_carry), .reset(RESET));  // open: D, Qn
  not not_11 (not_11_out, subtractor_1_bout);
  or or_1 (or_1_out, not_11_out, RESET);
  not not_12 (not_12_out, DONE);
  and and_1 (and_1_out, or_1_out, not_12_out);
  Multiplexer #(.enable("false"), .width(8)) multiplexer_1 (
    .in0(subtractor_1_out), .in1({4'b0000, Dividend}), .out(multiplexer_1_out), .sel(RESET));
  Subtractor subtractor_1 (
    .a({register_1_q, Remainder}), .b(shift_register_2_p16), .out(subtractor_1_out), .bin(1'b0),
    .bout(subtractor_1_bout));
  Register register_1 (
    .D(multiplexer_1_out), .en(and_1_out), .Q({register_1_q, Remainder}), .clk(clock_1_out));  // open: clr
  // Probe on Quotient
  // Probe on Remainder

  // Notes on the sheet:
  //   Sophie CAO, 260645315
endmodule
