// Logisim project SequentialMultipler.circ as structural Verilog: 1 circuit, main circuit Multiplier
module Multiplier (
  input  [3:0] A,
  input  [3:0] B,
  input  RESET,
  output [7:0] PRODUCT,
  output DONE
);

  wire clock_1_out, counter_1_carry, Multiplicand_p8, Multiplicand_p9, Multiplicand_p10, Multiplicand_p11,
       Multiplier_out, Multiplier_q0, Multiplier_q1, Multiplier_q2, not_5_out, or_1_out;
  wire [7:0] bitselector_1_out, Multiplicand_p12, register_1_q;

  // Probe on B
  // Probe on A
  Clock clock_1 (.out(clock_1_out));
  Shift_Register #(.length(4)) Multiplier (
    .in(RESET), .clk(clock_1_out), .out(Multiplier_out), .load(RESET), .d0(B[3]), .q0(Multiplier_q0),
    .d1(B[2]), .q1(Multiplier_q1), .d2(B[1]), .q2(Multiplier_q2), .d3(B[0]));  // open: shift, clr, q3
  Counter counter_1 (.carry(counter_1_carry), .up(1'b1), .clk(clock_1_out), .clr(RESET));  // open: load, D, count, Q
  or or_1 (or_1_out, Multiplier_q2, Multiplier_q1, Multiplier_q0);
  D_Flip_Flop d_ff_1 (.clk(clock_1_out), .preset(counter_1_carry), .reset(RESET));  // open: D, Q, Qn
  // Shift_Register Multiplicand: pin names not known; wires that end beside it: RESET, clock_1_out, RESET, A[0], A[1], A[2], A[3], Multiplicand_p8, Multiplicand_p9, Multiplicand_p10, Multiplicand_p11, Multiplicand_p12[0], Multiplicand_p12[1], Multiplicand_p12[2], Multiplicand_p12[3], Multiplicand_p12[4], Multiplicand_p12[5], Multiplicand_p12[6], Multiplicand_p12[7]
  not not_1 (Multiplicand_p8, RESET);
  not not_2 (Multiplicand_p9, RESET);
  not not_3 (Multiplicand_p10, RESET);
  not not_4 (Multiplicand_p11, RESET);
  Register register_1 (.D(PRODUCT), .Q(register_1_q), .clk(clock_1_out), .clr(RESET));  // open: en
  BitSelector #(.group(8)) bitselector_1 (.in(Multiplicand_p12), .out(bitselector_1_out), .sel(not_5_out));
  not not_5 (not_5_out, Multiplier_out);
  Adder adder_1 (.a(bitselector_1_out), .b(register_1_q), .out(PRODUCT));  // open: cin, cout
  // Probe on PRODUCT
  not not_6 (DONE, or_1_out);

  // Notes on the sheet:
  //   Sophie CAO, 260645315
endmodule
